# Fritzing sketch BlinkSimple one module (saved by Fritzing 0.9.3b)

parts:
  Part1 = Arduino Uno (Rev3) - ICSP
  Part3 = Arduino Uno (Rev3) - ICSP

nets:
  5V: Part1.5V, Part3.5V
  N1: Part1.D7, Part3.D7
  GND: Part1.GND, Part3.GND

notes:
  BlinkModuleMaster
  BlinkModule
  ModuleInterface example BlinkSimple
  Master controlling module's blink interval setting
  The master is changing the blink interval setting on a regular basis
  The module is simply blinking the built-in LED (pin 13) using the configured time interval setting
