# Fritzing sketch BlinkSimple two modules (saved by Fritzing 0.9.3b)

parts:
  Part1 = Arduino Uno (Rev3) - ICSP
  Part3 = Arduino Uno (Rev3) - ICSP
  Part4 = Arduino Uno (Rev3) - ICSP
  S1 = Pushbutton [package="[THT]"]

nets:
  N1: Part1.D7, Part3.D7, Part4.D7
  5V: Part1.5V, Part3.5V, Part4.5V
  GND: Part1.GND, Part3.GND, Part4.GND, S1.Pin_3
  N2: Part3.D8, S1.Pin_1

notes:
  BlinkModuleMaster
  BlinkModule or BlinkModuleEvent
  ModuleInterface example BlinkSimple
  Master controlling Blink module's interval setting, output from Blink controlling Follower
  The master is changing the blink interval setting on a regular basis
  BlinkModule is simply blinking the built-in LED (pin 13) using the configured time interval setting
  BlinkModuleFollower
  BlinkModuleEvent does the same but changes output to BlinkModuleFollower when pin 8 connects to ground, and transports it immediately as an event
  Push switch only for BlinkModuleEvent
