# Fritzing sketch ModuleMasterHttp (saved by Fritzing 0.9.3b)

parts:
  Part1 = Arduino Uno (Rev3) - ICSP  # not connected
  Part3 = Arduino Uno (Rev3) - ICSP
  Part4 = Arduino Ethernet Shield (Rev3)
  U1 = RJ45 Jack [package=rj45-8]  # not connected

nets:
  N1: Part3.D7, Part4.D7
  5V: Part3.5V, Part4.5V
  GND: Part3.GND, Part4.GND

notes:
  BlinkModuleMasterHttp on an Uno with Ethernet Shield
  BlinkModule
  ModuleInterface example BlinkMasterHttp
  Master controlling module's blink interval setting
  1. The master is changing the blink interval setting on a regular basis
  2. The module is using the setting from the master, and is reporting it back as an output
  3. The output from the module is transferred via HTTP to a web server where it is logged in a database
  Web server
