# Fritzing sketch ModuleInterfaceRGBSwitch (saved by Fritzing 0.9.3b)

parts:
  R1 = Resistor [tolerance=±5% resistance=8.2k package=THT]
  R2 = Resistor [tolerance=±5% resistance=33k package=THT]
  R3 = Resistor [tolerance=±5% resistance=23.3k package=THT]
  LED1 = RGB LED - (4 legs) [package="5 mm [THT]"]
  Part2 = Arduino Ethernet Shield (Rev3)
  Part3 = Arduino Mega ADK (Rev3)  # not connected

nets:
  N1: R1.Pin_0, Part2.PWM_D6
  N2: R2.Pin_0, Part2.PWM_D5
  N3: R3.Pin_0, Part2.SDCS
  N4: LED1.green_cathode, Part2.GND

notes:
  ModuleInterfaceRGBSwitch.ino on Arduino Mega+Ethernet
  Common cathode RGB LED
  ModuleInterface RGB Switch, LocalUDP <-> SWBB
  PJON SWBB bus
