# Fritzing sketch WebPage_hardware_setup (saved by Fritzing 0.9.3b)

parts:
  Part2 = Arduino Nano (Rev3.0)
  Part3 = Arduino Nano (Rev3.0)
  Part4 = Arduino Mega 2560 (Rev3)  # not connected
  Part5 = Arduino Ethernet Shield (Rev3)
  Grove1 = Grove Light Sensor
  S1 = Pushbutton [package="[SMD]"]

nets:
  GND: Part2.RESET, Part2.GND, Grove1.GND
  N1: Part2.D4, Part2.D5, Part2.D6, Part2.D7
  5V: Part2.5V, Grove1.VCC
  N2: Part2.A0, Grove1.SIG
  GND_2: Part3.GND, Part3.D4, Part5.GND, S1.Pin_3, S1.Pin_4
  N3: Part3.D7, Part5.D7
  VIN: Part3.VIN, Part5.VIN

notes:
  ModuleInterface WebPage demo setup v1.0
  SensorMonitor
  ModuleMasterHttp (Arduino Mega with Ethernet shield)
  LightController
  MI/PJON bus on yellow wire
  Web server on Windows/Linux
  Ethernet
  Supply voltage
  Local mode switch button (optional)
