# Fritzing sketch WebPage_hardware_setup (saved by Fritzing 0.9.3b)

parts:
  Grove1 = Grove Light Sensor
  WeMos_D1_Mini1 = WeMos D1 Mini
  WeMos_D1_Mini2 = WeMos D1 Mini  # not connected
  WeMos_D1_Mini3 = WeMos D1 Mini  # not connected

nets:
  N1: Grove1.GND, WeMos_D1_Mini1.G
  VCC: Grove1.VCC, WeMos_D1_Mini1.3V3
  N2: Grove1.SIG, WeMos_D1_Mini1.A0

notes:
  ModuleInterface WebPage demo setup v1.0
  SensorMonitor
  ModuleMasterHttp
  LightController
  Web server on Windows/Linux
  WiFi Ethernet
  WiFi router or access point
  Ethernet (cabled)
